# Fritzing sketch Schematic (saved by Fritzing 0.4.3b)
breadboards: 2

parts:
  Arduino1 = Arduino
  J1 = Basic Servo
  J1_2 = Basic Servo
  R1 = Resistor [resistance=1k package=THT]
  S2 = Pushbutton [package=THT]
  S2_2 = Pushbutton [package=THT]
  R1_2 = Resistor [resistance=1k package=THT]
  S3 = Toggle Switch [package=THT]
  S4 = Toggle Switch [package=THT]
  R1_3 = Resistor [resistance=1k package=THT]
  R1_4 = Resistor [resistance=1k package=THT]
  R1_5 = Resistor [resistance=1k package=THT]
  R1_6 = Resistor [resistance=1k package=THT]
  R1_7 = Resistor [resistance=1k package=THT]
  LED1 = RGB LED - (4 legs) [package="5 mm [THT]"]
  U1 = mystery part, 6 pins [chip_label=? spacing=300mil]  # not connected

nets:
  GND: Arduino1.GND, J1.gnd, J1_2.gnd, R1.Pin_0, R1_2.Pin_1, LED1.green_cathode
  N1: Arduino1.D13, R1_5.Pin_0
  N2: Arduino1.D12, R1_6.Pin_0
  N3: Arduino1.D11, R1_7.Pin_0
  N4: Arduino1.D7, J1.pulse
  N5: Arduino1.D6, J1_2.pulse
  N6: Arduino1.D5, S2_2.leg1, R1_4.Pin_0
  N7: Arduino1.D4, R1_2.Pin_0, S3.L2
  N8: Arduino1.D3, S4.L1, R1_3.Pin_0
  N9: Arduino1.D2, R1.Pin_1, S2.leg1
  VCC: Arduino1.+5V, J1.vcc, J1_2.vcc, S2.leg0, S2_2.leg0, S3.COM, S4.COM
  N10: R1_5.Pin_1, LED1.red_cathode
  N11: R1_6.Pin_1, LED1.common_anode
  N12: R1_7.Pin_1, LED1.blue_cathode

notes:
  Left = drink pin = red dot
  Right = train pin = microswitch
